// Logisim project Part A.circ as structural Verilog
module Ex1 (
  input  [7:0] in_1,
  output Out1,
  output [7:0] Out2
);

  not not_1 (Out2[7], in_1[7]);
  and and_1 (Out1, in_1[0], in_1[7]);

  assign Out2[6:0] = in_1[6:0];
endmodule

module Ex2 (
  input  [15:0] A,
  input  [3:0] B,
  output [15:0] C
);

  wire [15:0] _1_out_2, _2_out_2, _4_out_2, _8_out_2, multiplexer_1_out, multiplexer_2_out, multiplexer_3_out;

  Rotate1 _1 (.in_1(A), .out_2(_1_out_2));
  Multiplexer #(.width(16)) multiplexer_1 (.in0(A), .in1(_1_out_2), .out(multiplexer_1_out), .sel(B[0]));  // open: en
  Rotate2 _2 (.in_1(multiplexer_1_out), .out_2(_2_out_2));
  Multiplexer #(.width(16)) multiplexer_2 (
    .in0(multiplexer_1_out), .in1(_2_out_2), .out(multiplexer_2_out), .sel(B[1]));  // open: en
  Rotate4 _4 (.in_1(multiplexer_2_out), .out_2(_4_out_2));
  Multiplexer #(.width(16)) multiplexer_3 (
    .in0(multiplexer_2_out), .in1(_4_out_2), .out(multiplexer_3_out), .sel(B[2]));  // open: en
  Rotate8 _8 (.in_1(multiplexer_3_out), .out_2(_8_out_2));
  Multiplexer #(.width(16)) multiplexer_4 (.in0(multiplexer_3_out), .in1(_8_out_2), .out(C), .sel(B[3]));  // open: en
endmodule

module Rotate1 (
  input  [15:0] in_1,
  output [15:0] out_2
);


  assign out_2 = {in_1[0], in_1[15:1]};
endmodule

module Rotate2 (
  input  [15:0] in_1,
  output [15:0] out_2
);

  wire [15:0] rotate1_1_out_2;

  Rotate1 rotate1_1 (.in_1(in_1), .out_2(rotate1_1_out_2));
  Rotate1 rotate1_2 (.in_1(rotate1_1_out_2), .out_2(out_2));
endmodule

module Rotate4 (
  input  [15:0] in_1,
  output [15:0] out_2
);

  wire [15:0] rotate2_1_out_2;

  Rotate2 rotate2_1 (.in_1(in_1), .out_2(rotate2_1_out_2));
  Rotate2 rotate2_2 (.in_1(rotate2_1_out_2), .out_2(out_2));
endmodule

module Rotate8 (
  input  [15:0] in_1,
  output [15:0] out_2
);

  wire [15:0] rotate4_1_out_2;

  Rotate4 rotate4_1 (.in_1(in_1), .out_2(rotate4_1_out_2));
  Rotate4 rotate4_2 (.in_1(rotate4_1_out_2), .out_2(out_2));
endmodule
