// Logisim project Fib.circ as structural Verilog: 1 circuit, main circuit main
module main (
  input  [7:0] in_1,
  input  [7:0] in_2,
  output [15:0] out_3
);

  wire clock_1_out, comparator_1_lt;
  wire [7:0] adder_2_out, register_3_q;
  wire [15:0] register_1_q, register_2_q;

  Clock clock_1 (.out(clock_1_out));
  Register #(.width(16)) register_1 (
    .D(out_3), .en(comparator_1_lt), .Q(register_1_q), .clk(clock_1_out));  // open: clr
  Register #(.width(16)) register_2 (
    .D(register_1_q), .en(comparator_1_lt), .Q(register_2_q), .clk(clock_1_out));  // open: clr
  Adder #(.width(16)) adder_1 (.a(register_1_q), .b(register_2_q), .out(out_3));  // open: cin, cout
  Register register_3 (.D(adder_2_out), .Q(register_3_q), .clk(clock_1_out));  // open: en, clr
  Adder adder_2 (.a(in_1), .b(register_3_q), .out(adder_2_out));  // open: cin, cout
  // Probe on out_3
  Comparator comparator_1 (.a(register_3_q), .b(in_2), .lt(comparator_1_lt));  // open: gt, eq
endmodule
