// Logisim project cpu.circ as structural Verilog: 2 circuits, main circuit main
module main (
  input  [31:0] INSTRUCTION,
  input  CLOCK,
  output [31:0] FETCH_ADDRESS,
  output [31:0] s0_Value,
  output [31:0] s1_Value,
  output [31:0] s2_Value,
  output [31:0] ra_Value,
  output [31:0] sp_Value
);

  wire ALUSrc, beq, bne, bov, equ, ExtOp, j, jal, jalr, jr, lui, main_2_signed_overflow, main_3_p1,
       main_3_p3, main_3_p8, main_3_p12, MemToReg, MemWrite, nPC_sel, or_1_out, RegDst, RegWrite;
  wire [3:0] bit_extender_4_out;
  wire [4:0] multiplexer_3_out;
  wire [5:0] ALUCtr, funct, op;
  wire [15:6] imm;
  wire [25:16] j_addr;
  wire [31:0] adder_1_out, adder_2_out, bit_extender_1_out, bit_extender_2_out, bit_extender_3_out,
       bit_extender_5_out, main_1_read_data_1, main_1_read_data_2, main_2_result, main_3_p11,
       multiplexer_1_out, multiplexer_2_out, multiplexer_4_out, multiplexer_5_out, multiplexer_6_out,
       WriteValue;

  Multiplexer #(.width(32)) multiplexer_1 (
    .in0(INSTRUCTION), .in1({32{1'b0}}), .out(multiplexer_1_out), .sel(or_1_out));  // open: en
  or or_1 (or_1_out, beq, jr, bne, jalr, jal, bov, j);
  control Control (
    .op(op), .funct(funct), .RegDst(RegDst), .RegWrite(RegWrite), .ALUSrc(ALUSrc), .beq(beq), .jr(jr),
    .bne(bne), .bov(bov), .ALUCtr(ALUCtr), .lui(lui), .MemToReg(MemToReg), .MemWrite(MemWrite), .j(j),
    .jal(jal), .nPC_sel(nPC_sel), .ExtOp(ExtOp), .jalr(jalr));
  Register #(.width(32)) register_1 (
    .D(multiplexer_1_out), .Q({op, j_addr, imm, funct}), .clk(CLOCK));  // open: en, clr
  Adder #(.width(32)) adder_1 (.a(32'h4), .b(FETCH_ADDRESS), .out(adder_1_out));  // open: cin, cout
  Adder #(.width(32)) adder_2 (.a(adder_1_out), .b(bit_extender_1_out), .out(adder_2_out));  // open: cin, cout
  assign bit_extender_1_out = {{16{imm[15]}}, {imm, funct}};  // Bit_Extender bit_extender_1
  Multiplexer #(.width(32)) multiplexer_2 (
    .in0(adder_1_out), .in1(adder_2_out), .out(multiplexer_2_out), .sel(nPC_sel));  // open: en
  Multiplexer #(.width(5)) multiplexer_3 (
    .in0(j_addr[20:16]), .in1(imm[15:11]), .out(multiplexer_3_out), .sel(RegDst));  // open: en
  Register #(.width(32)) PC (.D(multiplexer_2_out), .Q(FETCH_ADDRESS), .clk(CLOCK));  // open: en, clr
  assign bit_extender_2_out = {{16{1'b0}}, {imm, funct}};  // Bit_Extender bit_extender_2
  assign bit_extender_3_out = {{16{imm[15]}}, {imm, funct}};  // Bit_Extender bit_extender_3
  regfile_main main_1 (
    .Read_Register_1(j_addr[25:21]), .Read_Register_2(j_addr[20:16]), .Write_Register(multiplexer_3_out),
    .Write_Data(WriteValue), .Write_Enable(RegWrite), .Clock(CLOCK), .Read_Data_1(main_1_read_data_1),
    .Read_Data_2(main_1_read_data_2), .s0_Value(s0_Value), .s1_Value(s1_Value), .s2_Value(s2_Value),
    .ra_Value(ra_Value), .sp_Value(sp_Value));
  Multiplexer #(.width(32)) multiplexer_4 (
    .in0(bit_extender_2_out), .in1(bit_extender_3_out), .out(multiplexer_4_out), .sel(ExtOp));  // open: en
  Multiplexer #(.width(32)) multiplexer_5 (
    .in0(main_1_read_data_2), .in1(multiplexer_4_out), .out(multiplexer_5_out), .sel(ALUSrc));  // open: en
  LED led_1 (.in(main_2_signed_overflow));
  alu_main main_2 (
    .Switch(bit_extender_4_out), .X(main_1_read_data_1), .Equal(equ), .Result(main_2_result),
    .Signed_Overflow(main_2_signed_overflow), .Y(multiplexer_5_out));
  Bit_Extender #(.in_width(6), .out_width(4)) bit_extender_4 (.in(ALUCtr), .out(bit_extender_4_out));
  assign bit_extender_5_out = {{16{1'b0}}, {imm, funct}};  // Bit_Extender bit_extender_5
  Multiplexer #(.width(32)) multiplexer_6 (
    .in0(main_2_result), .in1(bit_extender_5_out), .out(multiplexer_6_out), .sel(lui));  // open: en
  Multiplexer #(.width(32)) multiplexer_7 (
    .in0(multiplexer_6_out), .in1(main_3_p11), .out(WriteValue), .sel(MemToReg));  // open: en
  // mem_main main_3: pin names not known; wires that end beside it: main_3_p1, main_3_p1, main_3_p3, main_3_p3, main_2_result, main_1_read_data_2, MemWrite, main_3_p8, CLOCK, main_3_p8, main_3_p11, main_3_p12

  // Other names for the same wires on the sheet: imm[5:0] = funct; j_addr[15:0] = {imm, funct};
  //   shamt[4:0] = imm[10:6]; rd[4:0] = imm[15:11]; rt[4:0] = j_addr[20:16]; rs[4:0] = j_addr[25:21]; clk = CLOCK;
  //   fetch_addr[31:0] = FETCH_ADDRESS; ra[31:0] = ra_Value; s0[31:0] = s0_Value; s1[31:0] = s1_Value;
  //   s2[31:0] = s2_Value; sp[31:0] = sp_Value

  // Notes on the sheet:
  //   Output
  //   These are outputs/inputs from run.circ
  //   Inputs
  //   These are DEBUG/TEST outputs from your circuit.
endmodule

module control (
  input  [5:0] op,
  input  [5:0] funct,
  output RegDst,
  output RegWrite,
  output ALUSrc,
  output beq,
  output jr,
  output bne,
  output bov,
  output [5:0] ALUCtr,
  output lui,
  output MemToReg,
  output MemWrite,
  output j,
  output jal,
  output nPC_sel,
  output ExtOp,
  output jalr
);

  wire add, addi, addiu, addu, \and , andi, comparator_16_eq, comparator_17_eq, comparator_18_eq,
       comparator_19_eq, comparator_20_eq, comparator_21_eq, comparator_22_eq, comparator_23_eq,
       comparator_24_eq, comparator_25_eq, comparator_26_eq, comparator_27_eq, comparator_28_eq, \or , ori,
       sll, slt, slti, sltiu, sltu, sra, srl, sub, subu;

  Comparator #(.width(6)) comparator_1 (.a({6{1'b0}}), .b(op), .eq(RegDst));  // open: gt, lt
  Comparator #(.width(6)) comparator_2 (.a(6'b001000), .b(op), .eq(addi));  // open: gt, lt
  Comparator #(.width(6)) comparator_3 (.a(6'b001001), .b(op), .eq(addiu));  // open: gt, lt
  Comparator #(.width(6)) comparator_4 (.a(6'b001100), .b(op), .eq(andi));  // open: gt, lt
  Comparator #(.width(6)) comparator_5 (.a(6'b000100), .b(op), .eq(beq));  // open: gt, lt
  Comparator #(.width(6)) comparator_6 (.a(6'b000101), .b(op), .eq(bne));  // open: gt, lt
  Comparator #(.width(6)) comparator_7 (.a(6'b000110), .b(op), .eq(bov));  // open: gt, lt
  Comparator #(.width(6)) comparator_8 (.a(6'b001111), .b(op), .eq(lui));  // open: gt, lt
  Comparator #(.width(6)) comparator_9 (.a(6'b100011), .b(op), .eq(MemToReg));  // open: gt, lt
  Comparator #(.width(6)) comparator_10 (.a(6'b001101), .b(op), .eq(ori));  // open: gt, lt
  Comparator #(.width(6)) comparator_11 (.a(6'b001010), .b(op), .eq(slti));  // open: gt, lt
  Comparator #(.width(6)) comparator_12 (.a(6'b001011), .b(op), .eq(sltiu));  // open: gt, lt
  Comparator #(.width(6)) comparator_13 (.a(6'b101011), .b(op), .eq(MemWrite));  // open: gt, lt
  Comparator #(.width(6)) comparator_14 (.a(6'b000010), .b(op), .eq(j));  // open: gt, lt
  Comparator #(.width(6)) comparator_15 (.a(6'b000011), .b(op), .eq(jal));  // open: gt, lt
  or or_1 (nPC_sel, bne, beq, bov, j, jr, jal, jalr);
  or or_2 (ExtOp, addi, addiu, MemToReg, slti, sltiu, MemWrite);
  Comparator #(.width(6)) comparator_16 (.a(funct), .b(6'b001000), .eq(comparator_16_eq));  // open: gt, lt
  Comparator #(.width(6)) comparator_17 (.a(funct), .b(6'b101011), .eq(comparator_17_eq));  // open: gt, lt
  Comparator #(.width(6)) comparator_18 (.a(funct), .b(6'b100000), .eq(comparator_18_eq));  // open: gt, lt
  Comparator #(.width(6)) comparator_19 (.a(funct), .b(6'b100001), .eq(comparator_19_eq));  // open: gt, lt
  Comparator #(.width(6)) comparator_20 (.a(funct), .b(6'b100100), .eq(comparator_20_eq));  // open: gt, lt
  Comparator #(.width(6)) comparator_21 (.a(funct), .b(6'b100101), .eq(comparator_21_eq));  // open: gt, lt
  Comparator #(.width(6)) comparator_22 (.a(funct), .b(6'b101010), .eq(comparator_22_eq));  // open: gt, lt
  Comparator #(.width(6)) comparator_23 (.a(funct), .b({6{1'b0}}), .eq(comparator_23_eq));  // open: gt, lt
  Comparator #(.width(6)) comparator_24 (.a(funct), .b(6'b000011), .eq(comparator_24_eq));  // open: gt, lt
  Comparator #(.width(6)) comparator_25 (.a(funct), .b(6'b000010), .eq(comparator_25_eq));  // open: gt, lt
  Comparator #(.width(6)) comparator_26 (.a(funct), .b(6'b100010), .eq(comparator_26_eq));  // open: gt, lt
  Comparator #(.width(6)) comparator_27 (.a(funct), .b(6'b100011), .eq(comparator_27_eq));  // open: gt, lt
  Comparator #(.width(6)) comparator_28 (.a(funct), .b(6'b001001), .eq(comparator_28_eq));  // open: gt, lt
  or or_3 (RegWrite, addiu, addi, RegDst, andi, lui, MemToReg, ori, sltiu, slti);
  and and_1 (jr, RegDst, comparator_16_eq);
  and and_2 (sltu, comparator_17_eq, RegDst);
  and and_3 (add, comparator_18_eq, RegDst);
  and and_4 (addu, comparator_19_eq, RegDst);
  and and_5 (\and , comparator_20_eq, RegDst);
  and and_6 (\or , comparator_21_eq, RegDst);
  and and_7 (slt, comparator_22_eq, RegDst);
  and and_8 (sll, comparator_23_eq, RegDst);
  and and_9 (sra, comparator_24_eq, RegDst);
  and and_10 (srl, comparator_25_eq, RegDst);
  and and_11 (sub, comparator_26_eq, RegDst);
  and and_12 (subu, comparator_27_eq, RegDst);
  and and_13 (jalr, comparator_28_eq, RegDst);
  assign ALUCtr = add ? 6'b000101 : 6'bz;  // Controlled_Buffer controlled_buffer_1
  assign ALUCtr = addu ? 6'b000110 : 6'bz;  // Controlled_Buffer controlled_buffer_2
  assign ALUCtr = \and  ? 6'b001001 : 6'bz;  // Controlled_Buffer controlled_buffer_3
  assign ALUCtr = \or  ? 6'b010000 : 6'bz;  // Controlled_Buffer controlled_buffer_4
  assign ALUCtr = slt ? 6'b001011 : 6'bz;  // Controlled_Buffer controlled_buffer_5
  assign ALUCtr = sltu ? 6'b001100 : 6'bz;  // Controlled_Buffer controlled_buffer_6
  assign ALUCtr = sll ? {6{1'b0}} : 6'bz;  // Controlled_Buffer controlled_buffer_7
  assign ALUCtr = sra ? 6'b000010 : 6'bz;  // Controlled_Buffer controlled_buffer_8
  assign ALUCtr = srl ? 6'b000001 : 6'bz;  // Controlled_Buffer controlled_buffer_9
  assign ALUCtr = sub ? 6'b000111 : 6'bz;  // Controlled_Buffer controlled_buffer_10
  assign ALUCtr = subu ? 6'b001000 : 6'bz;  // Controlled_Buffer controlled_buffer_11
  or or_4 (ALUSrc, addi, lui, ori, andi, MemWrite, MemToReg, sltiu, slti, addiu);

  // Other names for the same wires on the sheet: lw = MemToReg; R = RegDst; sw = MemWrite
endmodule
