// Logisim project alu.circ as structural Verilog: 1 circuit, main circuit main
module main (
  input  [31:0] X,
  input  [31:0] Y,
  input  [3:0] Switch,
  output Signed_Overflow,
  output Equal,
  output [31:0] Result
);

  wire and_2_out, and_3_out, comparator_2_lt, comparator_3_lt, comparator_4_eq, comparator_5_lt,
       comparator_6_gt, comparator_7_eq, comparator_8_eq, multiplexer_2_out, not_1_out, xnor_1_out, xor_1_out;
  wire [4:0] bit_extender_1_out, bit_extender_2_out, bit_extender_3_out;
  wire [31:0] add, addu, \and , \or , sll, slt, sltu, sra, srl, sub, subu;

  Shifter #(.width(32)) shifter_1 (.in(Y), .\dist (bit_extender_1_out), .out(sll));
  Bit_Extender #(.in_width(32), .out_width(5)) bit_extender_1 (.in(X), .out(bit_extender_1_out));
  Shifter #(.width(32), .shift("lr")) shifter_2 (.in(Y), .\dist (bit_extender_2_out), .out(srl));
  Bit_Extender #(.in_width(32), .out_width(5)) bit_extender_2 (.in(X), .out(bit_extender_2_out));
  Shifter #(.width(32), .shift("ar")) shifter_3 (.in(Y), .\dist (bit_extender_3_out), .out(sra));
  Bit_Extender #(.in_width(32), .out_width(5)) bit_extender_3 (.in(X), .out(bit_extender_3_out));
  Adder #(.width(32)) adder_1 (.a(Y), .b(X), .out(add));  // open: cin, cout
  Adder #(.width(32)) adder_2 (.a(Y), .b(X), .out(addu));  // open: cin, cout
  Subtractor #(.width(32)) subtractor_1 (.a(X), .b(Y), .out(sub));  // open: bin, bout
  Comparator #(.width(32)) comparator_1 (.a(X), .b(Y), .eq(Equal));  // open: gt, lt
  Comparator #(.width(32), .mode("unsigned")) comparator_2 (.a(X), .b(Y), .lt(comparator_2_lt));  // open: gt, eq
  Comparator #(.width(32)) comparator_3 (.a(X), .b(Y), .lt(comparator_3_lt));  // open: gt, eq
  assign \or  = Y | X;  // OR_Gate or_1, 32 bits wide
  assign \and  = Y & X;  // AND_Gate and_1, 32 bits wide
  Subtractor #(.width(32)) subtractor_2 (.a(X), .b(Y), .out(subu));  // open: bin, bout
  assign sltu = {{31{1'b0}}, comparator_2_lt};  // Bit_Extender bit_extender_4
  assign slt = {{31{1'b0}}, comparator_3_lt};  // Bit_Extender bit_extender_5
  Multiplexer #(.select(4), .width(32)) multiplexer_1 (
    .in0(sll), .in1(srl), .in2(sra), .in5(add), .in6(addu), .in7(sub), .in8(subu), .in9(\and ), .in10(\or ),
    .in11(slt), .in12(sltu), .out(Result), .sel(Switch));  // open: in3, in4, in13, in14, in15, en
  xnor xnor_1 (xnor_1_out, X[31], Y[31]);
  Multiplexer multiplexer_2 (.in0(add[31]), .in1(X[31]), .out(multiplexer_2_out), .sel(xnor_1_out));  // open: en
  Comparator #(.width(4)) comparator_4 (.a(4'b0101), .b(Switch), .eq(comparator_4_eq));  // open: gt, lt
  Comparator #(.width(32)) comparator_5 (.a(sub), .b(X), .lt(comparator_5_lt));  // open: gt, eq
  Comparator #(.width(32)) comparator_6 (.a(Y), .b({32{1'b0}}), .gt(comparator_6_gt));  // open: eq, lt
  xor xor_1 (xor_1_out, multiplexer_2_out, add[31]);
  Comparator #(.width(1)) comparator_7 (
    .a(comparator_5_lt), .b(comparator_6_gt), .eq(comparator_7_eq));  // open: gt, lt
  and and_2 (and_2_out, not_1_out, comparator_8_eq);
  Comparator #(.width(4)) comparator_8 (.a(4'b0111), .b(Switch), .eq(comparator_8_eq));  // open: gt, lt
  and and_3 (and_3_out, xor_1_out, comparator_4_eq);
  not not_1 (not_1_out, comparator_7_eq);
  or or_2 (Signed_Overflow, and_3_out, and_2_out);

  // Other names for the same wires on the sheet: overflow = Signed_Overflow; S[3:0] = Switch

  // Notes on the sheet:
  //   INPUTS to your circuit
  //   DON'T CHANGE THE LOCATIONS OF THE INPUTS AND OUTPUTS!
  //   OUTPUTS from your circuit
endmodule
