// Logisim project regfile.circ as structural Verilog: 1 circuit, main circuit main
module main (
  input  [4:0] Read_Register_1,
  input  [4:0] Read_Register_2,
  input  [4:0] Write_Register,
  input  [31:0] Write_Data,
  input  Write_Enable,
  input  Clock,
  output [31:0] s0_Value,
  output [31:0] s1_Value,
  output [31:0] s2_Value,
  output [31:0] ra_Value,
  output [31:0] sp_Value,
  output [31:0] Read_Data_1,
  output [31:0] Read_Data_2
);

  wire and_1_out, demultiplexer_1_out0, demultiplexer_1_out1, demultiplexer_1_out2, demultiplexer_1_out3,
       demultiplexer_1_out4, demultiplexer_1_out5, demultiplexer_1_out6, demultiplexer_1_out7,
       demultiplexer_1_out8, demultiplexer_1_out9, demultiplexer_1_out10, demultiplexer_1_out11,
       demultiplexer_1_out12, demultiplexer_1_out13, demultiplexer_1_out14, demultiplexer_1_out15,
       demultiplexer_1_out16, demultiplexer_1_out17, demultiplexer_1_out18, demultiplexer_1_out19,
       demultiplexer_1_out20, demultiplexer_1_out21, demultiplexer_1_out22, demultiplexer_1_out23,
       demultiplexer_1_out24, demultiplexer_1_out25, demultiplexer_1_out26, demultiplexer_1_out27,
       demultiplexer_1_out28, demultiplexer_1_out29, demultiplexer_1_out30, demultiplexer_1_out31;
  wire [31:0] a0__4_q, a1__5_q, a2__6_q, a3__7_q, at__1_q, fp__30_q, gp__28_q, k0__26_q, k1__27_q, s3__19_q,
       s4__20_q, s5__21_q, s6__22_q, s7__23_q, t0__8_q, t1__9_q, t2__10_q, t3__11_q, t4__12_q, t5__13_q,
       t6__14_q, t7__15_q, t8__24_q, t9__25_q, v0__2_q, v1__3_q, zero__0_q;

  Demultiplexer #(.select(5)) demultiplexer_1 (
    .out0(demultiplexer_1_out0), .out1(demultiplexer_1_out1), .out2(demultiplexer_1_out2),
    .out3(demultiplexer_1_out3), .out4(demultiplexer_1_out4), .out5(demultiplexer_1_out5),
    .out6(demultiplexer_1_out6), .out7(demultiplexer_1_out7), .out8(demultiplexer_1_out8),
    .out9(demultiplexer_1_out9), .out10(demultiplexer_1_out10), .out11(demultiplexer_1_out11),
    .out12(demultiplexer_1_out12), .out13(demultiplexer_1_out13), .out14(demultiplexer_1_out14),
    .out15(demultiplexer_1_out15), .out16(demultiplexer_1_out16), .out17(demultiplexer_1_out17),
    .out18(demultiplexer_1_out18), .out19(demultiplexer_1_out19), .out20(demultiplexer_1_out20),
    .out21(demultiplexer_1_out21), .out22(demultiplexer_1_out22), .out23(demultiplexer_1_out23),
    .out24(demultiplexer_1_out24), .out25(demultiplexer_1_out25), .out26(demultiplexer_1_out26),
    .out27(demultiplexer_1_out27), .out28(demultiplexer_1_out28), .out29(demultiplexer_1_out29),
    .out30(demultiplexer_1_out30), .out31(demultiplexer_1_out31), .in(Write_Enable), .sel(Write_Register));  // open: en
  and and_1 (and_1_out, demultiplexer_1_out0, 1'b0);
  Register #(.width(32)) zero__0 (.D(Write_Data), .en(and_1_out), .Q(zero__0_q), .clk(Clock));  // open: clr
  Register #(.width(32)) at__1 (.D(Write_Data), .en(demultiplexer_1_out1), .Q(at__1_q), .clk(Clock));  // open: clr
  Register #(.width(32)) v0__2 (.D(Write_Data), .en(demultiplexer_1_out2), .Q(v0__2_q), .clk(Clock));  // open: clr
  Register #(.width(32)) v1__3 (.D(Write_Data), .en(demultiplexer_1_out3), .Q(v1__3_q), .clk(Clock));  // open: clr
  Register #(.width(32)) a0__4 (.D(Write_Data), .en(demultiplexer_1_out4), .Q(a0__4_q), .clk(Clock));  // open: clr
  Register #(.width(32)) a1__5 (.D(Write_Data), .en(demultiplexer_1_out5), .Q(a1__5_q), .clk(Clock));  // open: clr
  Register #(.width(32)) a2__6 (.D(Write_Data), .en(demultiplexer_1_out6), .Q(a2__6_q), .clk(Clock));  // open: clr
  Register #(.width(32)) a3__7 (.D(Write_Data), .en(demultiplexer_1_out7), .Q(a3__7_q), .clk(Clock));  // open: clr
  Register #(.width(32)) t0__8 (.D(Write_Data), .en(demultiplexer_1_out8), .Q(t0__8_q), .clk(Clock));  // open: clr
  Register #(.width(32)) t1__9 (.D(Write_Data), .en(demultiplexer_1_out9), .Q(t1__9_q), .clk(Clock));  // open: clr
  Register #(.width(32)) t2__10 (.D(Write_Data), .en(demultiplexer_1_out10), .Q(t2__10_q), .clk(Clock));  // open: clr
  Register #(.width(32)) t3__11 (.D(Write_Data), .en(demultiplexer_1_out11), .Q(t3__11_q), .clk(Clock));  // open: clr
  Register #(.width(32)) t4__12 (.D(Write_Data), .en(demultiplexer_1_out12), .Q(t4__12_q), .clk(Clock));  // open: clr
  Register #(.width(32)) t5__13 (.D(Write_Data), .en(demultiplexer_1_out13), .Q(t5__13_q), .clk(Clock));  // open: clr
  Register #(.width(32)) t6__14 (.D(Write_Data), .en(demultiplexer_1_out14), .Q(t6__14_q), .clk(Clock));  // open: clr
  Register #(.width(32)) t7__15 (.D(Write_Data), .en(demultiplexer_1_out15), .Q(t7__15_q), .clk(Clock));  // open: clr
  Register #(.width(32)) s0__16 (.D(Write_Data), .en(demultiplexer_1_out16), .Q(s0_Value), .clk(Clock));  // open: clr
  Register #(.width(32)) s1__17 (.D(Write_Data), .en(demultiplexer_1_out17), .Q(s1_Value), .clk(Clock));  // open: clr
  Register #(.width(32)) s2__18 (.D(Write_Data), .en(demultiplexer_1_out18), .Q(s2_Value), .clk(Clock));  // open: clr
  Register #(.width(32)) s3__19 (.D(Write_Data), .en(demultiplexer_1_out19), .Q(s3__19_q), .clk(Clock));  // open: clr
  Register #(.width(32)) s4__20 (.D(Write_Data), .en(demultiplexer_1_out20), .Q(s4__20_q), .clk(Clock));  // open: clr
  Register #(.width(32)) s5__21 (.D(Write_Data), .en(demultiplexer_1_out21), .Q(s5__21_q), .clk(Clock));  // open: clr
  Register #(.width(32)) s6__22 (.D(Write_Data), .en(demultiplexer_1_out22), .Q(s6__22_q), .clk(Clock));  // open: clr
  Register #(.width(32)) s7__23 (.D(Write_Data), .en(demultiplexer_1_out23), .Q(s7__23_q), .clk(Clock));  // open: clr
  Register #(.width(32)) t8__24 (.D(Write_Data), .en(demultiplexer_1_out24), .Q(t8__24_q), .clk(Clock));  // open: clr
  Register #(.width(32)) t9__25 (.D(Write_Data), .en(demultiplexer_1_out25), .Q(t9__25_q), .clk(Clock));  // open: clr
  Register #(.width(32)) k0__26 (.D(Write_Data), .en(demultiplexer_1_out26), .Q(k0__26_q), .clk(Clock));  // open: clr
  Register #(.width(32)) k1__27 (.D(Write_Data), .en(demultiplexer_1_out27), .Q(k1__27_q), .clk(Clock));  // open: clr
  Register #(.width(32)) gp__28 (.D(Write_Data), .en(demultiplexer_1_out28), .Q(gp__28_q), .clk(Clock));  // open: clr
  Register #(.width(32)) sp__29 (.D(Write_Data), .en(demultiplexer_1_out29), .Q(sp_Value), .clk(Clock));  // open: clr
  Register #(.width(32)) fp__30 (.D(Write_Data), .en(demultiplexer_1_out30), .Q(fp__30_q), .clk(Clock));  // open: clr
  Register #(.width(32)) ra__31 (.D(Write_Data), .en(demultiplexer_1_out31), .Q(ra_Value), .clk(Clock));  // open: clr
  Multiplexer #(.select(5), .width(32)) multiplexer_1 (
    .in0(zero__0_q), .in1(at__1_q), .in2(v0__2_q), .in3(v1__3_q), .in4(a0__4_q), .in5(a1__5_q),
    .in6(a2__6_q), .in7(a3__7_q), .in8(t0__8_q), .in9(t1__9_q), .in10(t2__10_q), .in11(t3__11_q),
    .in12(t4__12_q), .in13(t5__13_q), .in14(t6__14_q), .in15(t7__15_q), .in16(s0_Value), .in17(s1_Value),
    .in18(s2_Value), .in19(s3__19_q), .in20(s4__20_q), .in21(s5__21_q), .in22(s6__22_q), .in23(s7__23_q),
    .in24(t8__24_q), .in25(t9__25_q), .in26(k0__26_q), .in27(k1__27_q), .in28(gp__28_q), .in29(sp_Value),
    .in30(fp__30_q), .in31(ra_Value), .out(Read_Data_1), .sel(Read_Register_1));  // open: en
  Multiplexer #(.select(5), .width(32)) multiplexer_2 (
    .in0(zero__0_q), .in1(at__1_q), .in2(v0__2_q), .in3(v1__3_q), .in4(a0__4_q), .in5(a1__5_q),
    .in6(a2__6_q), .in7(a3__7_q), .in8(t0__8_q), .in9(t1__9_q), .in10(t2__10_q), .in11(t3__11_q),
    .in12(t4__12_q), .in13(t5__13_q), .in14(t6__14_q), .in15(t7__15_q), .in16(s0_Value), .in17(s1_Value),
    .in18(s2_Value), .in19(s3__19_q), .in20(s4__20_q), .in21(s5__21_q), .in22(s6__22_q), .in23(s7__23_q),
    .in24(t8__24_q), .in25(t9__25_q), .in26(k0__26_q), .in27(k1__27_q), .in28(gp__28_q), .in29(sp_Value),
    .in30(fp__30_q), .in31(ra_Value), .out(Read_Data_2), .sel(Read_Register_2));  // open: en

  // Other names for the same wires on the sheet: clk = Clock; read_data1[31:0] = Read_Data_1;
  //   read_data2[31:0] = Read_Data_2; read_reg1[4:0] = Read_Register_1; read_reg2[4:0] = Read_Register_2;
  //   write_en = Write_Enable; write_reg[4:0] = Write_Register

  // Notes on the sheet:
  //   INPUTS to your circuit
  //   DON'T CHANGE THE LOCATIONS OF THE INPUTS AND OUTPUTS!
  //   These are DEBUG/TEST outputs from your circuit.
  //   OUTPUTS from your circuit
endmodule
